# Fritzing sketch arduino_lcd (saved by Fritzing 0.9.3b)
breadboards: 1

parts:
  LCD1 = LCD screen
  Part1 = Arduino Nano (Rev3.0)
  R1 = Resistor [tolerance=±5% resistance=220 package=THT]

nets:
  VSS: LCD1.VSS, LCD1.LED-, Part1.GND, R1.Pin_1
  VDD: LCD1.VDD, LCD1.R/W, LCD1.LED+, Part1.5V
  N1: LCD1.V0, R1.Pin_0
  N2: LCD1.RS, Part1.D12/MISO
  N3: LCD1.E, Part1.D11/MOSI
  N4: LCD1.DB4, Part1.D4
  N5: LCD1.DB5, Part1.D5
  N6: LCD1.DB6, Part1.D6
  N7: LCD1.DB7, Part1.D7
