# Fritzing sketch arduino_esp8266 (saved by Fritzing 0.9.3b)
breadboards: 1

parts:
  U1 = ESP8266 WiFi Module [part_number=ESP8266]
  Part1 = Arduino Uno (Rev3)

nets:
  N1: U1.RXD, Part1.D2
  VCC: U1.VCC, U1.CH_PD, Part1.3V3
  GND: U1.GND, Part1.GND
  N2: U1.TXD, Part1.D3_PWM

custom parts:
  ESP8266 WiFi Module: Generic WiFi Module based on the ESP8266 with onboard PCB antenna and UART communications
